// Logisim project Tic-Tac-Toe.circ as structural Verilog: 11 circuits, main circuit main
module main (
  output [7:0] out_1,
  output [3:0] out_2
);

  wire and_1_out, B1, B2, B3, B4, B5, B6, B7, B8, B9, button_1_out, ButtonOn, cdm_8_1_p2, cdm_8_1_p4,
       cdm_8_1_p5, cdm_8_1_p6, cdm_8_1_p7, cdm_8_1_p8, cdm_8_1_p9, cdm_8_1_p10, cdm_8_1_p11, cl, code, data,
       I_Osel, in_out, nand_1_out, not_1_out, not_2_out, not_3_out, pull_resistor_6_node,
       pull_resistor_7_node, RAM, rd_rw;
  wire [3:0] cdm_8_1_p13, or_2_out, pull_resistor_1_node, pull_resistor_2_node, pull_resistor_4_node,
       pull_resistor_5_node;
  wire [7:0] cdm_8_1_p14, cdm_8_1_p15, controlled_buffer_11_out, displayreg1_1_value, displayreg2_1_value,
       displayreg3_1_value, displayreg4_1_value, displayreg5_1_value, displayreg6_1_value,
       displayreg7_1_value, displayreg8_1_value, displayreg9_1_value;
  wire [7:4] cdm_8_1_p13_2;
  wire [8:0] _11, _12, _13, _14, _15, _21, _22, _23, _24, _25, _31, _32, _33, _34, _35, _41, _42, _43, _44,
       _45, _51, _52, _53, _54, _55, _61, _62, _63, _64, _65, _71, _72, _73, _74, _75, _81, _82, _83, _84,
       _85, _91, _92, _93, _94, _95;

  DotMatrix #(.matrixcols(9), .matrixrows(9)) dotmatrix_1 (
    .col0(_11), .col1(_12), .col2(_13), .col3(_14), .col4(_15), .col5(_14), .col6(_13), .col7(_12), .col8(_11));
  DotMatrix #(.matrixcols(9), .matrixrows(9)) dotmatrix_2 (
    .col0(_41), .col1(_42), .col2(_43), .col3(_44), .col4(_45), .col5(_44), .col6(_43), .col7(_42), .col8(_41));
  DotMatrix #(.matrixcols(9), .matrixrows(9)) dotmatrix_3 (
    .col0(_71), .col1(_72), .col2(_73), .col3(_74), .col4(_75), .col5(_74), .col6(_73), .col7(_72), .col8(_71));
  Clock clock_1 ();  // open: out
  // Probe on cdm_8_1_p2
  Button button_1 (.out(button_1_out));
  Clock clock_2 ();  // open: out
  assign in_out = not_1_out ? rd_rw : 1'bz;  // Controlled_Buffer controlled_buffer_1
  assign out_2 = not_1_out ? cdm_8_1_p13 : 4'bz;  // Controlled_Buffer controlled_buffer_2
  assign I_Osel = not_1_out ? and_1_out : 1'bz;  // Controlled_Buffer controlled_buffer_3
  and and_1 (and_1_out, not_2_out, cl, data);
  assign out_1 = not_1_out ? controlled_buffer_11_out : 8'bz;  // Controlled_Buffer controlled_buffer_4
  not not_1 (not_1_out, ButtonOn);
  Button button_2 (.out(B1));
  Button button_3 (.out(B2));
  Button button_4 (.out(B4));
  Button button_5 (.out(B5));
  Button button_6 (.out(B8));
  Button button_7 (.out(B7));
  // Probe on cdm_8_1_p6
  // Probe on cdm_8_1_p4
  // Probe on cdm_8_1_p5
  not not_2 (not_2_out, nand_1_out);
  DotMatrix #(.matrixcols(9), .matrixrows(9)) dotmatrix_4 (
    .col0(_21), .col1(_22), .col2(_23), .col3(_24), .col4(_25), .col5(_24), .col6(_23), .col7(_22), .col8(_21));
  DotMatrix #(.matrixcols(9), .matrixrows(9)) dotmatrix_5 (
    .col0(_51), .col1(_52), .col2(_53), .col3(_54), .col4(_55), .col5(_54), .col6(_53), .col7(_52), .col8(_51));
  DotMatrix #(.matrixcols(9), .matrixrows(9)) dotmatrix_6 (
    .col0(_81), .col1(_82), .col2(_83), .col3(_84), .col4(_85), .col5(_84), .col6(_83), .col7(_82), .col8(_81));
  Button button_8 (.out(B3));
  Button button_9 (.out(B6));
  Button button_10 (.out(B9));
  // Probe on cdm_8_1_p9
  // Probe on cdm_8_1_p8
  // Probe on cdm_8_1_p7
  nand nand_1 (nand_1_out, cdm_8_1_p13_2[4], cdm_8_1_p13_2[5], cdm_8_1_p13_2[6], cdm_8_1_p13_2[7]);
  and and_2 (RAM, nand_1_out, data);
  DotMatrix #(.matrixcols(9), .matrixrows(9)) dotmatrix_7 (
    .col0(_31), .col1(_32), .col2(_33), .col3(_34), .col4(_35), .col5(_34), .col6(_33), .col7(_32), .col8(_31));
  DotMatrix #(.matrixcols(9), .matrixrows(9)) dotmatrix_8 (
    .col0(_61), .col1(_62), .col2(_63), .col3(_64), .col4(_65), .col5(_64), .col6(_63), .col7(_62), .col8(_61));
  DotMatrix #(.matrixcols(9), .matrixrows(9)) dotmatrix_9 (
    .col0(_91), .col1(_92), .col2(_93), .col3(_94), .col4(_95), .col5(_94), .col6(_93), .col7(_92), .col8(_91));
  assign out_1 = ButtonOn ? 8'h3 : 8'bz;  // Controlled_Buffer controlled_buffer_5
  or or_1 (ButtonOn, B1, B2, B3, B4);
  assign or_2_out = pull_resistor_2_node | pull_resistor_1_node | pull_resistor_5_node | pull_resistor_4_node;  // OR_Gate or_2, 4 bits wide
  Pull_Resistor pull_resistor_1 (.node(pull_resistor_1_node));
  Pull_Resistor pull_resistor_2 (.node(pull_resistor_2_node));
  assign pull_resistor_1_node = B2 ? 4'b0001 : 4'bz;  // Controlled_Buffer controlled_buffer_6
  assign pull_resistor_2_node = B1 ? 4'b0000 : 4'bz;  // Controlled_Buffer controlled_buffer_7
  Decoder #(.disabled(0)) decoder_1 (.out0(code), .out1(data), .sel(cdm_8_1_p10), .en(cdm_8_1_p11));
  // CdM_8 cdm_8_1: pin names not known; wires that end beside it: cl, cdm_8_1_p2, button_1_out, cdm_8_1_p4, cdm_8_1_p5, cdm_8_1_p6, cdm_8_1_p7, cdm_8_1_p8, cdm_8_1_p9, cdm_8_1_p10, cdm_8_1_p11, rd_rw, {cdm_8_1_p13_2, cdm_8_1_p13}, cdm_8_1_p14, cdm_8_1_p15
  assign cdm_8_1_p15 = rd_rw ? controlled_buffer_11_out : 8'bz;  // Controlled_Buffer controlled_buffer_8
  Pull_Resistor pull_resistor_3 (.node(or_2_out));
  Pull_Resistor pull_resistor_4 (.node(pull_resistor_4_node));
  Pull_Resistor pull_resistor_5 (.node(pull_resistor_5_node));
  assign pull_resistor_5_node = B3 ? 4'b0010 : 4'bz;  // Controlled_Buffer controlled_buffer_9
  assign pull_resistor_4_node = B4 ? 4'b0011 : 4'bz;  // Controlled_Buffer controlled_buffer_10
  assign controlled_buffer_11_out = not_3_out ? cdm_8_1_p14 : 8'bz;  // Controlled_Buffer controlled_buffer_11
  not not_3 (not_3_out, rd_rw);
  Pull_Resistor #(.pull(1)) pull_resistor_6 (.node(pull_resistor_6_node));
  Pull_Resistor pull_resistor_7 (.node(pull_resistor_7_node));
  Pull_Resistor pull_resistor_8 (.node(cdm_8_1_p13[0]));
  Pull_Resistor pull_resistor_9 (.node(cdm_8_1_p13[1]));
  Pull_Resistor pull_resistor_10 (.node(cdm_8_1_p13[2]));
  Pull_Resistor pull_resistor_11 (.node(cdm_8_1_p13[3]));
  Pull_Resistor pull_resistor_12 (.node(cdm_8_1_p13_2[4]));
  Pull_Resistor pull_resistor_13 (.node(cdm_8_1_p13_2[5]));
  Pull_Resistor pull_resistor_14 (.node(cdm_8_1_p13_2[6]));
  Pull_Resistor pull_resistor_15 (.node(cdm_8_1_p13_2[7]));
  DisplayReg1 displayreg1_1 (
    .in_out(in_out), .I_Odat(out_1), .value(displayreg1_1_value), .I_Oadr(out_2), .I_Osel(I_Osel));
  assign I_Osel = ButtonOn ? pull_resistor_6_node : 1'bz;  // Controlled_Buffer controlled_buffer_12
  assign in_out = ButtonOn ? pull_resistor_7_node : 1'bz;  // Controlled_Buffer controlled_buffer_13
  ROM rom_1 (.addr({cdm_8_1_p13_2, cdm_8_1_p13}), .data(controlled_buffer_11_out), .sel(code));
  RAM ram_1 (
    .addr({cdm_8_1_p13_2, cdm_8_1_p13}), .data(controlled_buffer_11_out), .sel(RAM), .clk(cl), .ld(rd_rw));  // open: clr
  DisplayReg2 displayreg2_1 (
    .in_out(in_out), .I_Odat(out_1), .value(displayreg2_1_value), .I_Oadr(out_2), .I_Osel(I_Osel));
  assign out_2 = ButtonOn ? or_2_out : 4'bz;  // Controlled_Buffer controlled_buffer_14
  DisplayReg3 displayreg3_1 (
    .in_out(in_out), .I_Odat(out_1), .value(displayreg3_1_value), .I_Oadr(out_2), .I_Osel(I_Osel));
  DisplayReg4 displayreg4_1 (
    .in_out(in_out), .I_Odat(out_1), .value(displayreg4_1_value), .I_Oadr(out_2), .I_Osel(I_Osel));
  DisplayControl displaycontrol_1 (
    .\input (displayreg2_1_value), .outSignals_1_2({_22, _21}), .outSignals_3_4_5({_25, _24, _23}));
  DisplayControl displaycontrol_2 (
    .\input (displayreg1_1_value), .outSignals_1_2({_12, _11}), .outSignals_3_4_5({_15, _14, _13}));
  DisplayControl displaycontrol_3 (
    .\input (displayreg3_1_value), .outSignals_1_2({_32, _31}), .outSignals_3_4_5({_35, _34, _33}));
  DisplayReg9 displayreg9_1 (
    .in_out(in_out), .I_Odat(out_1), .value(displayreg9_1_value), .I_Oadr(out_2), .I_Osel(I_Osel));
  DisplayControl displaycontrol_4 (
    .\input (displayreg9_1_value), .outSignals_1_2({_92, _91}), .outSignals_3_4_5({_95, _94, _93}));
  DisplayControl displaycontrol_5 (
    .\input (displayreg4_1_value), .outSignals_1_2({_42, _41}), .outSignals_3_4_5({_45, _44, _43}));
  DisplayReg8 displayreg8_1 (
    .in_out(in_out), .I_Odat(out_1), .value(displayreg8_1_value), .I_Oadr(out_2), .I_Osel(I_Osel));
  DisplayControl displaycontrol_6 (
    .\input (displayreg8_1_value), .outSignals_1_2({_82, _81}), .outSignals_3_4_5({_85, _84, _83}));
  DisplayControl displaycontrol_7 (
    .\input (displayreg7_1_value), .outSignals_1_2({_72, _71}), .outSignals_3_4_5({_75, _74, _73}));
  DisplayControl displaycontrol_8 (
    .\input (displayreg6_1_value), .outSignals_1_2({_62, _61}), .outSignals_3_4_5({_65, _64, _63}));
  DisplayReg6 displayreg6_1 (
    .in_out(in_out), .I_Odat(out_1), .value(displayreg6_1_value), .I_Oadr(out_2), .I_Osel(I_Osel));
  DisplayReg7 displayreg7_1 (
    .in_out(in_out), .I_Odat(out_1), .value(displayreg7_1_value), .I_Oadr(out_2), .I_Osel(I_Osel));
  DisplayControl displaycontrol_9 (
    .\input (displayreg5_1_value), .outSignals_1_2({_52, _51}), .outSignals_3_4_5({_55, _54, _53}));
  DisplayReg5 displayreg5_1 (
    .in_out(in_out), .I_Odat(out_1), .value(displayreg5_1_value), .I_Oadr(out_2), .I_Osel(I_Osel));

  // Other names for the same wires on the sheet: I_Oadr[3:0] = out_2; I_Odat[7:0] = out_1

  // Notes on the sheet:
  //   contents of rom_1 (hex, n*v repeats v):
  //   d0 f0 d1 2 a1 8c a1 8c a1 8c a1 8c a1 8c a1 8c a1 8c a1 8c a1 d0 f0 d1 3 a1 8c a1 8c a1 8c a1 8c a1
  //   8c a1 8c a1 8c a1 8c a1 d4
  //   2
  //   3
  //   1
  //   9
  //   4
  //   7
  //   6
  //   8
  //   5
endmodule

module DisplayControl (
  input  [7:0] \input ,
  output [17:0] outSignals_1_2,
  output [26:0] outSignals_3_4_5
);

  Multiplexer #(.width(18), .disabled(0)) multiplexer_1 (
    .in0(18'h202fe), .in1(18'h10501), .out(outSignals_1_2), .sel(\input [0]), .en(\input [1]));
  Pull_Resistor pull_resistor_1 (.node(outSignals_1_2));
  Multiplexer #(.width(27), .disabled(0)) multiplexer_2 (
    .in0(27'h4060301), .in1(27'h405044), .out(outSignals_3_4_5), .sel(\input [0]), .en(\input [1]));
  Pull_Resistor pull_resistor_2 (.node(outSignals_3_4_5));
endmodule

module DisplayReg1 (
  input  I_Osel,
  input  [3:0] I_Oadr,
  input  in_out,
  input  [7:0] I_Odat,
  output [7:0] value
);

  wire and_1_out, decoder_1_out0, decoder_1_out1;

  Register register_1 (.D(I_Odat), .Q(value), .clk(decoder_1_out0));  // open: en, clr
  assign I_Odat = decoder_1_out1 ? value : 8'bz;  // Controlled_Buffer controlled_buffer_1
  and and_1 (and_1_out, ~I_Oadr[3], ~I_Oadr[2], ~I_Oadr[1], ~I_Oadr[0], I_Osel);  // AND_Gate
  Decoder #(.disabled(0)) decoder_1 (.out0(decoder_1_out0), .out1(decoder_1_out1), .sel(in_out), .en(and_1_out));
endmodule

module DisplayReg2 (
  input  I_Osel,
  input  [3:0] I_Oadr,
  input  in_out,
  input  [7:0] I_Odat,
  output [7:0] value
);

  wire and_1_out, decoder_1_out0, decoder_1_out1;

  Register register_1 (.D(I_Odat), .Q(value), .clk(decoder_1_out0));  // open: en, clr
  assign I_Odat = decoder_1_out1 ? value : 8'bz;  // Controlled_Buffer controlled_buffer_1
  and and_1 (and_1_out, ~I_Oadr[3], ~I_Oadr[2], ~I_Oadr[1], I_Oadr[0], I_Osel);  // AND_Gate
  Decoder #(.disabled(0)) decoder_1 (.out0(decoder_1_out0), .out1(decoder_1_out1), .sel(in_out), .en(and_1_out));
endmodule

module DisplayReg3 (
  input  I_Osel,
  input  [3:0] I_Oadr,
  input  in_out,
  input  [7:0] I_Odat,
  output [7:0] value
);

  wire and_1_out, decoder_1_out0, decoder_1_out1;

  Register register_1 (.D(I_Odat), .Q(value), .clk(decoder_1_out0));  // open: en, clr
  assign I_Odat = decoder_1_out1 ? value : 8'bz;  // Controlled_Buffer controlled_buffer_1
  and and_1 (and_1_out, ~I_Oadr[3], ~I_Oadr[2], I_Oadr[1], ~I_Oadr[0], I_Osel);  // AND_Gate
  Decoder #(.disabled(0)) decoder_1 (.out0(decoder_1_out0), .out1(decoder_1_out1), .sel(in_out), .en(and_1_out));
endmodule

module DisplayReg4 (
  input  I_Osel,
  input  [3:0] I_Oadr,
  input  in_out,
  input  [7:0] I_Odat,
  output [7:0] value
);

  wire and_1_out, decoder_1_out0, decoder_1_out1;

  Register register_1 (.D(I_Odat), .Q(value), .clk(decoder_1_out0));  // open: en, clr
  assign I_Odat = decoder_1_out1 ? value : 8'bz;  // Controlled_Buffer controlled_buffer_1
  and and_1 (and_1_out, ~I_Oadr[3], ~I_Oadr[2], I_Oadr[1], I_Oadr[0], I_Osel);  // AND_Gate
  Decoder #(.disabled(0)) decoder_1 (.out0(decoder_1_out0), .out1(decoder_1_out1), .sel(in_out), .en(and_1_out));
endmodule

module DisplayReg5 (
  input  I_Osel,
  input  [3:0] I_Oadr,
  input  in_out,
  input  [7:0] I_Odat,
  output [7:0] value
);

  wire and_1_out, decoder_1_out0, decoder_1_out1;

  Register register_1 (.D(I_Odat), .Q(value), .clk(decoder_1_out0));  // open: en, clr
  assign I_Odat = decoder_1_out1 ? value : 8'bz;  // Controlled_Buffer controlled_buffer_1
  and and_1 (and_1_out, ~I_Oadr[3], I_Oadr[2], ~I_Oadr[1], ~I_Oadr[0], I_Osel);  // AND_Gate
  Decoder #(.disabled(0)) decoder_1 (.out0(decoder_1_out0), .out1(decoder_1_out1), .sel(in_out), .en(and_1_out));
endmodule

module DisplayReg6 (
  input  I_Osel,
  input  [3:0] I_Oadr,
  input  in_out,
  input  [7:0] I_Odat,
  output [7:0] value
);

  wire and_1_out, decoder_1_out0, decoder_1_out1;

  Register register_1 (.D(I_Odat), .Q(value), .clk(decoder_1_out0));  // open: en, clr
  assign I_Odat = decoder_1_out1 ? value : 8'bz;  // Controlled_Buffer controlled_buffer_1
  and and_1 (and_1_out, ~I_Oadr[3], I_Oadr[2], ~I_Oadr[1], I_Oadr[0], I_Osel);  // AND_Gate
  Decoder #(.disabled(0)) decoder_1 (.out0(decoder_1_out0), .out1(decoder_1_out1), .sel(in_out), .en(and_1_out));
endmodule

module DisplayReg7 (
  input  I_Osel,
  input  [3:0] I_Oadr,
  input  in_out,
  input  [7:0] I_Odat,
  output [7:0] value
);

  wire and_1_out, decoder_1_out0, decoder_1_out1;

  Register register_1 (.D(I_Odat), .Q(value), .clk(decoder_1_out0));  // open: en, clr
  assign I_Odat = decoder_1_out1 ? value : 8'bz;  // Controlled_Buffer controlled_buffer_1
  and and_1 (and_1_out, ~I_Oadr[3], I_Oadr[2], I_Oadr[1], ~I_Oadr[0], I_Osel);  // AND_Gate
  Decoder #(.disabled(0)) decoder_1 (.out0(decoder_1_out0), .out1(decoder_1_out1), .sel(in_out), .en(and_1_out));
endmodule

module DisplayReg8 (
  input  I_Osel,
  input  [3:0] I_Oadr,
  input  in_out,
  input  [7:0] I_Odat,
  output [7:0] value
);

  wire and_1_out, decoder_1_out0, decoder_1_out1;

  Register register_1 (.D(I_Odat), .Q(value), .clk(decoder_1_out0));  // open: en, clr
  assign I_Odat = decoder_1_out1 ? value : 8'bz;  // Controlled_Buffer controlled_buffer_1
  and and_1 (and_1_out, ~I_Oadr[3], I_Oadr[2], I_Oadr[1], I_Oadr[0], I_Osel);  // AND_Gate
  Decoder #(.disabled(0)) decoder_1 (.out0(decoder_1_out0), .out1(decoder_1_out1), .sel(in_out), .en(and_1_out));
endmodule

module DisplayReg9 (
  input  I_Osel,
  input  [3:0] I_Oadr,
  input  in_out,
  input  [7:0] I_Odat,
  output [7:0] value
);

  wire and_1_out, decoder_1_out0, decoder_1_out1;

  Register register_1 (.D(I_Odat), .Q(value), .clk(decoder_1_out0));  // open: en, clr
  assign I_Odat = decoder_1_out1 ? value : 8'bz;  // Controlled_Buffer controlled_buffer_1
  and and_1 (and_1_out, I_Oadr[3], ~I_Oadr[2], ~I_Oadr[1], ~I_Oadr[0], I_Osel);  // AND_Gate
  Decoder #(.disabled(0)) decoder_1 (.out0(decoder_1_out0), .out1(decoder_1_out1), .sel(in_out), .en(and_1_out));
endmodule
